// Logisim project RegFile.circ as structural Verilog: 3 circuits, main circuit main
module main (
  input  [3:0] dIn,
  input  [3:0] XSel,
  input  [3:0] YSel,
  input  [3:0] wSel,
  output [3:0] dbgA,
  output [3:0] dbgB,
  output [3:0] dbgC,
  output [3:0] dbgD,
  output [3:0] XOut,
  output [3:0] YOut
);

  // Reg_4 reg_4_1: pin names not known; wires that end beside it: dIn, wSel[3], dbgA
  // Reg_4 reg_4_2: pin names not known; wires that end beside it: dIn, wSel[2], dbgB
  // Reg_4 reg_4_3: pin names not known; wires that end beside it: dIn, wSel[1], dbgC
  // Reg_4 reg_4_4: pin names not known; wires that end beside it: dIn, wSel[0], dbgD
  Sel sel_1 (.A(dbgA), .B(dbgB), .C(dbgC), .D(dbgD), .Out(XOut), .Sel(XSel));
  Sel sel_2 (.A(dbgA), .B(dbgB), .C(dbgC), .D(dbgD), .Out(YOut), .Sel(YSel));
endmodule

module Sel (
  input  [3:0] A,
  input  [3:0] B,
  input  [3:0] C,
  input  [3:0] D,
  input  [3:0] Sel,
  output [3:0] Out
);

  assign Out = Sel[3] ? A : 4'bz;  // Controlled_Buffer controlled_buffer_1
  assign Out = Sel[2] ? B : 4'bz;  // Controlled_Buffer controlled_buffer_2
  assign Out = Sel[1] ? C : 4'bz;  // Controlled_Buffer controlled_buffer_3
  assign Out = Sel[0] ? D : 4'bz;  // Controlled_Buffer controlled_buffer_4
endmodule

module dSel (
  input  [3:0] ALUIn,
  input  [3:0] RAMIn,
  input  Sel,
  output [3:0] Out
);

  Multiplexer #(.width(4), .enable("false")) multiplexer_1 (.in0(ALUIn), .in1(RAMIn), .out(Out), .sel(Sel));
endmodule
